// Digital circuit batalhaNaval.dig as structural Verilog
module batalhaNaval (
  input  [3:0] pos_navio,
  input  [3:0] Alvo,
  input  [3:0] pos_navio_2,
  input  [3:0] Alvo_2
);

  wire button_1_out, button_2_out, button_3_out, button_4_out, Disparo_2_out, Disparo_out, prox_nav_2_out,
       prox_nav_out, u_BatalhaNaval_2_acertou, u_BatalhaNaval_2_derota, u_BatalhaNaval_2_errou,
       u_BatalhaNaval_2_led_1, u_BatalhaNaval_2_led_2, u_BatalhaNaval_2_led_3a, u_BatalhaNaval_2_led_3b,
       u_BatalhaNaval_2_vitoria, u_BatalhaNaval_acertou, u_BatalhaNaval_derota, u_BatalhaNaval_errou,
       u_BatalhaNaval_led_1, u_BatalhaNaval_led_2, u_BatalhaNaval_led_3a, u_BatalhaNaval_led_3b,
       u_BatalhaNaval_led_disp, u_BatalhaNaval_vitoria, u_disp7seg_2_a, u_disp7seg_2_b, u_disp7seg_2_c,
       u_disp7seg_2_d, u_disp7seg_2_e, u_disp7seg_2_f, u_disp7seg_2_g, u_disp7seg_2_h, u_disp7seg_a,
       u_disp7seg_b, u_disp7seg_c, u_disp7seg_d, u_disp7seg_e, u_disp7seg_f, u_disp7seg_g, u_disp7seg_h;
  wire [3:0] u_BatalhaNaval_2_display, u_BatalhaNaval_display;

  Button prox_nav (.out(prox_nav_out));
  Button button_1 (.out(button_1_out));
  Button button_2 (.out(button_2_out));
  Button Disparo (.out(Disparo_out));
  Button prox_nav_2 (.out(prox_nav_2_out));
  Button button_3 (.out(button_3_out));
  Button button_4 (.out(button_4_out));
  Button Disparo_2 (.out(Disparo_2_out));
  BatalhaNaval #(.applicationType("GHDL")) u_BatalhaNaval (
    .navio(pos_navio), .clock(prox_nav_out), .navio_prox(button_1_out), .reset(button_2_out),
    .disparar(Disparo_out), .alvo(Alvo), .acertou(u_BatalhaNaval_acertou), .errou(u_BatalhaNaval_errou),
    .led_1(u_BatalhaNaval_led_1), .led_2(u_BatalhaNaval_led_2), .led_3a(u_BatalhaNaval_led_3a),
    .led_3b(u_BatalhaNaval_led_3b), .led_disp(u_BatalhaNaval_led_disp), .display(u_BatalhaNaval_display),
    .vitoria(u_BatalhaNaval_vitoria), .derota(u_BatalhaNaval_derota));
  BatalhaNaval #(.applicationType("GHDL")) u_BatalhaNaval_2 (
    .navio(pos_navio_2), .clock(prox_nav_2_out), .navio_prox(button_3_out), .reset(button_4_out),
    .disparar(Disparo_2_out), .alvo(Alvo_2), .acertou(u_BatalhaNaval_2_acertou),
    .errou(u_BatalhaNaval_2_errou), .led_1(u_BatalhaNaval_2_led_1), .led_2(u_BatalhaNaval_2_led_2),
    .led_3a(u_BatalhaNaval_2_led_3a), .led_3b(u_BatalhaNaval_2_led_3b), .display(u_BatalhaNaval_2_display),
    .vitoria(u_BatalhaNaval_2_vitoria), .derota(u_BatalhaNaval_2_derota));
  LED led_1 (.in(u_BatalhaNaval_acertou));
  LED led_2 (.in(u_BatalhaNaval_errou));
  LED led_3 (.in(u_BatalhaNaval_led_1));
  LED led_4 (.in(u_BatalhaNaval_led_2));
  LED led_5 (.in(u_BatalhaNaval_led_3a));
  LED led_6 (.in(u_BatalhaNaval_led_3b));
  LED led_7 (.in(u_BatalhaNaval_led_disp));
  LED led_8 (.in(u_BatalhaNaval_vitoria));
  LED led_9 (.in(u_BatalhaNaval_derota));
  LED led_10 (.in(u_BatalhaNaval_2_acertou));
  LED led_11 (.in(u_BatalhaNaval_2_errou));
  LED led_12 (.in(u_BatalhaNaval_2_led_1));
  LED led_13 (.in(u_BatalhaNaval_2_led_2));
  LED led_14 (.in(u_BatalhaNaval_2_led_3a));
  LED led_15 (.in(u_BatalhaNaval_2_led_3b));
  LED led_16 (.in(u_BatalhaNaval_2_vitoria));
  LED led_17 (.in(u_BatalhaNaval_2_derota));
  disp7seg #(.applicationType("GHDL")) u_disp7seg (
    .Data_In(u_BatalhaNaval_display), .a(u_disp7seg_a), .b(u_disp7seg_b), .c(u_disp7seg_c), .d(u_disp7seg_d),
    .e(u_disp7seg_e), .f(u_disp7seg_f), .g(u_disp7seg_g), .h(u_disp7seg_h));  // open: dig_uni, dig_dez, dig_cen, dig_mil
  disp7seg #(.applicationType("GHDL")) u_disp7seg_2 (
    .Data_In(u_BatalhaNaval_2_display), .a(u_disp7seg_2_a), .b(u_disp7seg_2_b), .c(u_disp7seg_2_c),
    .d(u_disp7seg_2_d), .e(u_disp7seg_2_e), .f(u_disp7seg_2_f), .g(u_disp7seg_2_g), .h(u_disp7seg_2_h));  // open: dig_uni, dig_dez, dig_cen, dig_mil
  Seven_Seg seven_seg_1 (
    .a(u_disp7seg_a), .b(u_disp7seg_b), .c(u_disp7seg_c), .d(u_disp7seg_d), .e(u_disp7seg_e),
    .f(u_disp7seg_f), .g(u_disp7seg_g), .dp(u_disp7seg_h));
  Seven_Seg seven_seg_2 (
    .a(u_disp7seg_2_a), .b(u_disp7seg_2_b), .c(u_disp7seg_2_c), .d(u_disp7seg_2_d), .e(u_disp7seg_2_e),
    .f(u_disp7seg_2_f), .g(u_disp7seg_2_g), .dp(u_disp7seg_2_h));
endmodule

/* Code of BatalhaNaval:
library ieee;
use ieee.std_logic_1164.all;

-- Definição da entidade
entity BatalhaNaval is
    port (
        -- Entradas do dono do mar
        navio : in std_logic_vector(3 downto 0);
        clock : in std_logic;
        navio_prox: in std_logic;
        reset : in std_logic;
        disparar : in std_logic;
        alvo : in std_logic_vector(3 downto 0);

        
        -- Saídas
        acertou : out std_logic;
        errou : out std_logic;
        led_1 : out std_logic;
        led_2 : out std_logic;
        led_3a : out std_logic;
        led_3b : out std_logic;
        led_disp : out std_logic;
        display : out std_logic_vector(3 downto 0);
        vitoria : out std_logic;
        derota  : out std_logic
    
        --display_seg   : out std_logic_vector(6 downto 0)

    );
end entity BatalhaNaval;

architecture mainBatalhaNaval of BatalhaNaval is
        type Navio_Type is (navio_1,navio_2,navio_3a,navio_3b,disp);
        signal navio_atual: Navio_Type := navio_1;
    
         -- Sinais internos
    signal navio_pos :integer range 0 to 16;
    signal navio_1_pos :integer range 0 to 16;
    signal navio_2_pos :integer range 0 to 16;
    signal navio_3_pos1 :integer range 0 to 16;
    signal navio_3_pos2 :integer range 0 to 16;
    signal pos_alvo : integer range 0 to 15;
    signal num_disparos : integer range 0 to 10:=6;
    signal num_vitorias : integer range 0 to 3;
    signal num_derotas : integer range 0 to 10;


    
    begin
        --selecao dos navios 
        process(clock,reset)
            variable count: integer := 0;
        begin
            if reset = '1' then
                navio_atual <= navio_1;
            elsif clock'event and clock = '1' then
                count := count + 1;
                if count = 1 then 
                    navio_atual <= navio_1;
                elsif count = 2 then 
                    navio_atual <= navio_2;
                elsif count = 3 then 
                    navio_atual <= navio_3a;
                elsif count = 4 then 
                    navio_atual <= navio_3b;
                elsif count = 5 then 
                    navio_atual <= disp;
                end if;
            end if;
        end process;
        
        --codifficacao das posicoes  dos navios 
        process(navio)
        begin
            if navio =  "1011" then
                navio_pos <= 0;
            elsif navio =  "1000" then
                navio_pos <= 1;
            elsif navio =  "1110" then
                navio_pos <= 2;
            elsif navio =  "1100" then
                navio_pos <= 3;
            elsif navio =  "0011" then
                navio_pos <= 4;
            elsif navio =  "0000" then
                navio_pos <= 5;
            elsif navio =  "0010" then
                navio_pos <= 6;
            elsif navio =  "1101" then
                navio_pos <= 7;
            elsif navio =  "1111" then
                navio_pos <= 8;
            elsif navio =  "0110" then
                navio_pos <= 9;
            elsif navio =  "0100" then
                navio_pos <= 10;
            elsif navio =  "1001" then
                navio_pos <= 11;
            elsif navio =  "0111" then
                navio_pos <= 12;
            elsif navio =  "0101" then
                navio_pos <= 13;
            elsif navio =  "0001" then
                navio_pos <= 14;
            elsif navio =  "1010" then
                navio_pos <= 15;
            end if;
        end process;


        -- atribuiçao das posições 
        process(navio_atual)
            begin
                case navio_atual is 
                    when navio_1 =>
                        led_1 <= '1';
                        led_2 <= '0';
                        led_3a <= '0';
                        led_3b <= '0';
                        navio_1_pos <= navio_pos;
                    when navio_2 =>
                        led_1 <= '0';
                        led_2 <= '1';
                        led_3a <= '0';
                        led_3b <= '0';
                        navio_2_pos <= navio_pos;
                    when navio_3a =>
                        led_1 <= '0';
                        led_2 <= '0';
                        led_3a <= '1';
                        led_3b <= '0';
                        navio_3_pos1 <= navio_pos;
                    when navio_3b =>
                        led_1 <= '0';
                        led_2 <= '0';
                        led_3a <= '0';
                        led_3b <= '1';
                        navio_3_pos2 <= navio_pos;
                    when disp =>
                        led_1 <= '0';
                        led_2 <= '0';
                        led_3a <= '0';
                        led_3b <= '0';
                        led_disp <= '1';
                    when others =>
                        led_1 <= '0';
                        led_2 <= '0';
                        led_3a <= '0';
                        led_3b <= '0';
                        led_disp <= '1';
                end case;
        end process;

        
        -- codificacao das posições do alvo
        process(alvo,pos_alvo)
            begin
                if alvo =  "1100" then
                    pos_alvo <=0;
                elsif alvo = "1101" then
                    pos_alvo <= 1;
                elsif alvo = "1110" then
                    pos_alvo <= 2;
                elsif alvo = "1111" then
                    pos_alvo <= 3;
                elsif alvo = "1000" then
                    pos_alvo <= 4;
                elsif alvo = "1001" then
                    pos_alvo <= 5;
                elsif alvo = "1010" then
                    pos_alvo <= 6;
                elsif alvo = "1011" then
                    pos_alvo <= 7;
                elsif alvo = "0100" then
                    pos_alvo <= 8;
                elsif alvo = "0101" then
                    pos_alvo <= 9;
                elsif alvo = "0110" then
                    pos_alvo <= 10;
                elsif alvo = "0111" then
                    pos_alvo <= 11;
                elsif alvo = "0000" then
                    pos_alvo <= 12;
                elsif alvo = "0001" then
                    pos_alvo <= 13;
                elsif alvo = "0010" then
                    pos_alvo <= 14;
                elsif alvo = "0011" then
                    pos_alvo <= 15;
                end if;
        end process;

        -- processo para comparar e disparar
        process(navio_1_pos, navio_2_pos, navio_3_pos1, navio_3_pos2, disparar)
            variable contador : integer range 0 to 2 := 0;
            begin
                acertou <= '0';
                errou <= '0';
                if disparar'event and disparar = '1' then
                    if num_disparos = 1 then 
                        if pos_alvo = navio_1_pos  then
                            acertou <= '1';
                            --num_disparos <= num_disparos - 1;
                            num_vitorias <= num_vitorias + 1;
                            --navio_1_pos <= 16;
                        elsif pos_alvo = navio_2_pos  then
                            acertou <= '1';
                            --num_disparos <= num_disparos - 1;
                            num_vitorias <= num_vitorias + 1;
                            --navio_2_pos <= 16;
                        elsif pos_alvo = navio_3_pos1 or pos_alvo = navio_3_pos2 then
                            contador := contador + 1;
                            if contador = 2 then
                                acertou <= '1';
                                --num_disparos <= num_disparos - 1;
                                num_vitorias <= num_vitorias + 1;
                            -- navio_3_pos1 <= 16;
                            -- navio_3_pos2 <= 16;
                            end if;
                        else
                            errou <= '1';
                            num_disparos <= num_disparos - 1;
                        end if;
                    else 
                        if pos_alvo = navio_1_pos  then
                            acertou <= '1';
                            num_disparos <= num_disparos - 1;
                            num_vitorias <= num_vitorias + 1;
                            --navio_1_pos <= 16;
                        elsif pos_alvo = navio_2_pos  then
                            acertou <= '1';
                            num_disparos <= num_disparos - 1;
                            num_vitorias <= num_vitorias + 1;
                            --navio_2_pos <= 16;
                        elsif pos_alvo = navio_3_pos1 or pos_alvo = navio_3_pos2 then
                            contador := contador + 1;
                            if contador = 2 then
                                acertou <= '1';
                                num_disparos <= num_disparos - 1;
                                num_vitorias <= num_vitorias + 1;
                            -- navio_3_pos1 <= 16;
                            -- navio_3_pos2 <= 16;
                            end if;
                        else
                            errou <= '1';
                            num_disparos <= num_disparos - 1;
                        end if;
                    end if;
                end if;
        end process;
    
        -- Processo para determinar o resultado do jogo e exibir o número de disparos no display
    process(num_disparos)
    begin
        case num_disparos is
            when 0 =>
                display <= "0000";
            when 1 =>
                display <= "0001";
            when 2 =>
                display <= "0010";
            when 3 =>
                display <= "0011";
            when 4 =>
                display <= "0100";
            when 5 =>
                display <= "0101";
            when 6 =>
                display <= "0110";
            --when 11 =>
              --  display <= "1011";
            when others =>
                display <= "1011"; -- Exemplo: manter o último número de disparos exibido
        end case;
    end process;

    process(num_disparos,num_vitorias,num_derotas)
        begin
            if num_vitorias = 3 then 
                vitoria <= '1';
            end if;
            if num_disparos = 0 and num_vitorias < 3 then
                derota <= '1';
            end if;
    end process;

end architecture mainBatalhaNaval;
*/

/* Code of BatalhaNaval:
library ieee;
use ieee.std_logic_1164.all;

-- Definição da entidade
entity BatalhaNaval is
    port (
        -- Entradas do dono do mar
        navio : in std_logic_vector(3 downto 0);
        clock : in std_logic;
        navio_prox: in std_logic;
        reset : in std_logic;
        disparar : in std_logic;
        alvo : in std_logic_vector(3 downto 0);

        
        -- Saídas
        acertou : out std_logic;
        errou : out std_logic;
        led_1 : out std_logic;
        led_2 : out std_logic;
        led_3a : out std_logic;
        led_3b : out std_logic;
        display : out std_logic_vector(3 downto 0);
        vitoria : out std_logic;
        derota  : out std_logic
    
        --display_seg   : out std_logic_vector(6 downto 0)

    );
end entity BatalhaNaval;

architecture mainBatalhaNaval of BatalhaNaval is
        type Navio_Type is (navio_1,navio_2,navio_3a,navio_3b);
        signal navio_atual: Navio_Type := navio_1;
    
         -- Sinais internos
    signal navio_pos :integer range 0 to 16;
    signal navio_1_pos :integer range 0 to 16;
    signal navio_2_pos :integer range 0 to 16;
    signal navio_3_pos1 :integer range 0 to 16;
    signal navio_3_pos2 :integer range 0 to 16;
    signal pos_alvo : integer range 0 to 15;
    signal num_disparos : integer range 0 to 15:=10;
    signal num_vitorias : integer range 0 to 3;
    signal num_derotas : integer range 0 to 10;


    
    begin
        --selecao dos navios 
        process(clock,reset)
            variable count: integer := 0;
        begin
            if reset = '1' then
                navio_atual <= navio_1;
            elsif clock'event and clock = '1' then
                count := count + 1;
                if count = 1 then 
                    navio_atual <= navio_1;
                elsif count = 2 then 
                    navio_atual <= navio_2;
                elsif count = 3 then 
                    navio_atual <= navio_3a;
                elsif count = 4 then 
                    navio_atual <= navio_3b;
                end if;
            end if;
        end process;
        
        --codifficacao das posicoes  dos navios 
        process(navio)
        begin
            if navio =  "1011" then
                navio_pos <= 0;
            elsif navio =  "1000" then
                navio_pos <= 1;
            elsif navio =  "1110" then
                navio_pos <= 2;
            elsif navio =  "1100" then
                navio_pos <= 3;
            elsif navio =  "0011" then
                navio_pos <= 4;
            elsif navio =  "0000" then
                navio_pos <= 5;
            elsif navio =  "0010" then
                navio_pos <= 6;
            elsif navio =  "1101" then
                navio_pos <= 7;
            elsif navio =  "1111" then
                navio_pos <= 8;
            elsif navio =  "0110" then
                navio_pos <= 9;
            elsif navio =  "0100" then
                navio_pos <= 10;
            elsif navio =  "1001" then
                navio_pos <= 11;
            elsif navio =  "0111" then
                navio_pos <= 12;
            elsif navio =  "0101" then
                navio_pos <= 13;
            elsif navio =  "0001" then
                navio_pos <= 14;
            elsif navio =  "1010" then
                navio_pos <= 15;
            end if;
        end process;


        -- atribuiçao das posições 
        process(navio_atual)
            begin
                case navio_atual is 
                    when navio_1 =>
                        led_1 <= '1';
                        led_2 <= '0';
                        led_3a <= '0';
                        led_3b <= '0';
                        navio_1_pos <= navio_pos;
                    when navio_2 =>
                        led_1 <= '0';
                        led_2 <= '1';
                        led_3a <= '0';
                        led_3b <= '0';
                        navio_2_pos <= navio_pos;
                    when navio_3a =>
                        led_1 <= '0';
                        led_2 <= '0';
                        led_3a <= '1';
                        led_3b <= '0';
                        navio_3_pos1 <= navio_pos;
                    when navio_3b =>
                        led_1 <= '0';
                        led_2 <= '0';
                        led_3a <= '0';
                        led_3b <= '1';
                        navio_3_pos2 <= navio_pos;
                end case;
        end process;

        
        -- codificacao das posições do alvo
        process(alvo,pos_alvo)
            begin
                if alvo =  "1100" then
                    pos_alvo <=0;
                elsif alvo = "1101" then
                    pos_alvo <= 1;
                elsif alvo = "1110" then
                    pos_alvo <= 2;
                elsif alvo = "1111" then
                    pos_alvo <= 3;
                elsif alvo = "1000" then
                    pos_alvo <= 4;
                elsif alvo = "1001" then
                    pos_alvo <= 5;
                elsif alvo = "1010" then
                    pos_alvo <= 6;
                elsif alvo = "1011" then
                    pos_alvo <= 7;
                elsif alvo = "0100" then
                    pos_alvo <= 8;
                elsif alvo = "0101" then
                    pos_alvo <= 9;
                elsif alvo = "0110" then
                    pos_alvo <= 10;
                elsif alvo = "0111" then
                    pos_alvo <= 11;
                elsif alvo = "0000" then
                    pos_alvo <= 12;
                elsif alvo = "0001" then
                    pos_alvo <= 13;
                elsif alvo = "0010" then
                    pos_alvo <= 14;
                elsif alvo = "0011" then
                    pos_alvo <= 15;
                end if;
        end process;

        -- processo para comparar e disparar
        process(navio_1_pos, navio_2_pos, navio_3_pos1, navio_3_pos2, disparar)
            variable contador : integer range 0 to 2 := 0;
            begin
                acertou <= '0';
                errou <= '0';
                if disparar'event and disparar = '1' then
                    if num_disparos = 1 then 
                        if pos_alvo = navio_1_pos  then
                            acertou <= '1';
                            --num_disparos <= num_disparos - 1;
                            num_vitorias <= num_vitorias + 1;
                            --navio_1_pos <= 16;
                        elsif pos_alvo = navio_2_pos  then
                            acertou <= '1';
                            --num_disparos <= num_disparos - 1;
                            num_vitorias <= num_vitorias + 1;
                            --navio_2_pos <= 16;
                        elsif pos_alvo = navio_3_pos1 or pos_alvo = navio_3_pos2 then
                            contador := contador + 1;
                            if contador = 2 then
                                acertou <= '1';
                                --num_disparos <= num_disparos - 1;
                                num_vitorias <= num_vitorias + 1;
                            -- navio_3_pos1 <= 16;
                            -- navio_3_pos2 <= 16;
                            end if;
                        else
                            errou <= '1';
                            num_disparos <= num_disparos - 1;
                        end if;
                    else 
                        if pos_alvo = navio_1_pos  then
                            acertou <= '1';
                            num_disparos <= num_disparos - 1;
                            num_vitorias <= num_vitorias + 1;
                            --navio_1_pos <= 16;
                        elsif pos_alvo = navio_2_pos  then
                            acertou <= '1';
                            num_disparos <= num_disparos - 1;
                            num_vitorias <= num_vitorias + 1;
                            --navio_2_pos <= 16;
                        elsif pos_alvo = navio_3_pos1 or pos_alvo = navio_3_pos2 then
                            contador := contador + 1;
                            if contador = 2 then
                                acertou <= '1';
                                num_disparos <= num_disparos - 1;
                                num_vitorias <= num_vitorias + 1;
                            -- navio_3_pos1 <= 16;
                            -- navio_3_pos2 <= 16;
                            end if;
                        else
                            errou <= '1';
                            num_disparos <= num_disparos - 1;
                        end if;
                    end if;
                end if;
        end process;
    
        -- Processo para determinar o resultado do jogo e exibir o número de disparos no display
    process(num_disparos)
    begin
        case num_disparos is
            when 0 =>
                display <= "0000";
            when 1 =>
                display <= "0001";
            when 2 =>
                display <= "0010";
            when 3 =>
                display <= "0011";
            when 4 =>
                display <= "0100";
            when 5 =>
                display <= "0101";
            when 6 =>
                display <= "0110";
            when 7 =>
                display <= "0111";
            when 8 =>
                display <= "1000";
            when 9 =>
                display <= "1001";
            when 10 =>
                display <= "1010";
            --when 11 =>
              --  display <= "1011";
            when others =>
                display <= "1011"; -- Exemplo: manter o último número de disparos exibido
        end case;
    end process;

    process(num_disparos,num_vitorias,num_derotas)
        begin
            if num_vitorias = 3 then 
                vitoria <= '1';
            end if;
            if num_disparos = 0 and num_vitorias < 3 then
                derota <= '1';
            end if;
    end process;

end architecture mainBatalhaNaval;
*/

/* Code of disp7seg:
library ieee;
	use ieee.std_logic_1164.all;
	use ieee.std_logic_arith.all;
	use ieee.std_logic_unsigned.all;
	
	
	entity disp7seg is
	port(
	    Data_In          :   in  std_logic_vector(3 downto 0);
        a,b,c,d,e,f,g,h  :  out  std_logic;
		dig_uni          :  out  std_logic;
        dig_dez          :  out  std_logic;
        dig_cen          :  out  std_logic;
        dig_mil          :  out  std_logic);
		  
   end disp7seg;
	
	
	architecture hardware of disp7seg is
	begin
		process(Data_In)
		begin
		  case Data_In is
		  when "0000"   => a <= '1'; b <= '1'; c <= '1'; d <= '1'; e <= '1'; f <= '1'; g <= '0'; h <= '0';
	      when "0001"   => a <= '0'; b <= '1'; c <= '1'; d <= '0'; e <= '0'; f <= '0'; g <= '0'; h <= '0';
	      when "0010"   => a <= '1'; b <= '1'; c <= '0'; d <= '1'; e <= '1'; f <= '0'; g <= '1'; h <= '0';	
	      when "0011"   => a <= '1'; b <= '1'; c <= '1'; d <= '1'; e <= '0'; f <= '0'; g <= '1'; h <= '0'; 
	      when "0100"   => a <= '0'; b <= '1'; c <= '1'; d <= '0'; e <= '0'; f <= '1'; g <= '1'; h <= '0';	
	      when "0101"   => a <= '1'; b <= '0'; c <= '1'; d <= '1'; e <= '0'; f <= '1'; g <= '1'; h <= '0';	
	      when "0110"   => a <= '1'; b <= '0'; c <= '1'; d <= '1'; e <= '1'; f <= '1'; g <= '1'; h <= '0';	
	      when "0111"   => a <= '1'; b <= '1'; c <= '1'; d <= '0'; e <= '0'; f <= '0'; g <= '0'; h <= '0';	
	      when "1000"   => a <= '1'; b <= '1'; c <= '1'; d <= '1'; e <= '1'; f <= '1'; g <= '1'; h <= '0';
	      when "1001"   => a <= '1'; b <= '1'; c <= '1'; d <= '1'; e <= '0'; f <= '1'; g <= '1'; h <= '0';			
	      when others   => a <= '0'; b <= '0'; c <= '0'; d <= '0'; e <= '0'; f <= '0'; g <= '0'; h <= '0';	
	     end case;
		end process;
		
		dig_mil <= '1';
		dig_cen <= '1';
		dig_dez <= '1';
		dig_uni <= '1';
		
		
   end hardware;
*/
